# Fritzing sketch Led_pulsador (saved by Fritzing 0.9.3b)
breadboards: 1

parts:
  part = Arduino Uno (Rev3)
  R1 = Resistor [tolerance=±5% resistance=220 package=THT]
  LED1 = LED - 5mm [color="Red (633nm)" package="5 mm [THT]"]
  S1 = Momentary Switch [package=ksa_sealed_tac_switch]
  R2 = Resistor [tolerance=±5% resistance=10k package=THT]

nets (from the schematic view):
  N1: part.D11_PWM/MOSI, LED1.anode
  N2: part.GND, R1.Pin_1, R2.Pin_0
  N3: part.D2, S1.4
  N4: part.5V, S1.2
  N5: S1.3, R2.Pin_1
